// Logisim project ordi_logic.circ as structural Verilog: 9 circuits, main circuit main
module main (
);

  wire and_1_out, and_2_out, and_3_out, and_4_out, and_5_out, and_6_out, and_7_out, and_8_out, and_9_out,
       and_10_out, and_11_out, and_12_out, and_13_out, and_14_out, and_15_out, button_1_out, clock_1_out,
       compare_2_out_2, decoder_1_out0, decoder_1_out1, decoder_1_out2, decoder_1_out3, decoder_2_out3,
       nand_1_out, not_1_out, not_2_out, not_3_out, not_4_out, not_5_out, not_6_out, not_7_out, not_8_out,
       or_1_out, or_2_out, or_3_out, or_4_out, or_5_out, sequencer_1_out_3, sequencer_1_out_4,
       sequencer_1_out_5, sequencer_1_out_6, sequencer_2_out_3, sequencer_2_out_4, sequencer_2_out_5,
       sequencer_2_out_6;
  wire [0:0] compare_1_out_2;
  wire [2:0] rom_1_data_2, rom_1_data_4;
  wire [6:0] keyboard_1_data;
  wire [7:0] adder_1_out, ALU_out_3, register_1_q, register_3_out_2, transistor_1_out, transistor_7_out,
       transistor_13_out, transistor_15_out;
  wire [15:0] register_5_q, transistor_3_out, transistor_9_out;
  wire [15:8] register_2_q, rom_1_data_3;
  wire [15:11] rom_1_data_5;
  wire [31:0] rom_1_data;

  Register register_1 (.D(transistor_1_out), .Q(register_1_q), .clk(clock_1_out));  // open: en, clr
  Adder adder_1 (.a(register_1_q), .b(8'h1), .out(adder_1_out));  // open: cin, cout
  Transistor #(.\type ("n"), .width(8)) transistor_1 (.in(adder_1_out), .out(transistor_1_out), .gate(and_1_out));
  Transistor #(.\type ("n"), .width(8)) transistor_2 (.in(register_5_q[15:8]), .out(transistor_1_out), .gate(or_3_out));
  ROM #(.dataWidth(32)) rom_1 (
    .addr(register_1_q),
    .data({rom_1_data[31:27], rom_1_data_2, rom_1_data_3, rom_1_data_5, rom_1_data_4, rom_1_data[7:0]}));  // open: sel
  Clock clock_1 (.out(clock_1_out));
  or or_1 (or_1_out, not_3_out, decoder_1_out1, decoder_1_out2, and_2_out);
  and and_1 (and_1_out, sequencer_2_out_6, or_1_out);
  and and_2 (and_2_out, decoder_1_out3, sequencer_1_out_4, not_1_out);
  not not_1 (not_1_out, or_3_out);
  and and_3 (and_3_out, not_2_out, decoder_1_out2);
  ALU ALU (.in_1({4'b0000, rom_1_data[27], rom_1_data_2, register_5_q}), .out_3(ALU_out_3));  // open: out_2
  Decoder #(.select(2)) decoder_1 (
    .out0(decoder_1_out0), .out1(decoder_1_out1), .out2(decoder_1_out2), .out3(decoder_1_out3),
    .sel(rom_1_data[31:30]));  // open: en
  not not_2 (not_2_out, rom_1_data[27]);
  or or_2 (or_2_out, decoder_1_out0, decoder_1_out1);
  and and_4 (and_4_out, decoder_1_out2, rom_1_data[27]);
  TTY tty_1 (.data(keyboard_1_data), .clk(clock_1_out), .we(clock_1_out), .clr(button_1_out));
  Keyboard keyboard_1 (.clk(clock_1_out), .data(keyboard_1_data));  // open: re, clr, avail
  Button button_1 (.out(button_1_out));
  not not_3 (not_3_out, nand_1_out);
  nand nand_1 (nand_1_out, sequencer_2_out_6, or_2_out);
  and and_5 (and_5_out, sequencer_2_out_4, decoder_1_out3);
  Decoder #(.select(2)) decoder_2 (.out3(decoder_2_out3), .sel(rom_1_data_2[1:0]));  // open: out0, out1, out2, en
  compare compare_1 (.in_1({{5{1'b0}}, rom_1_data_2, register_5_q}), .out_2(compare_1_out_2[0]));
  Register register_2 (.D(transistor_7_out), .en(sequencer_1_out_3), .Q(register_2_q), .clk(clock_1_out));  // open: clr
  compare compare_2 (.in_1({{5{1'b0}}, rom_1_data_2, register_2_q, {8{1'b0}}}), .out_2(compare_2_out_2));
  sequencer sequencer_1 (
    .in_1(and_5_out), .out_3(sequencer_1_out_3), .out_4(sequencer_1_out_4), .out_5(sequencer_1_out_5),
    .out_6(sequencer_1_out_6), .in_2(and_4_out));
  not not_4 (not_4_out, decoder_2_out3);
  and and_6 (and_6_out, compare_2_out_2, sequencer_1_out_4);
  Transistor #(.\type ("n"), .width(16)) transistor_3 (
    .in({16{1'b0}}), .out(transistor_3_out), .gate(sequencer_1_out_3));
  or or_3 (or_3_out, and_9_out, and_7_out);
  and and_7 (and_7_out, sequencer_1_out_4, decoder_1_out3, decoder_2_out3);
  not not_5 (not_5_out, or_4_out);
  Transistor #(.\type ("n"), .width(16)) transistor_4 (.in({16{1'b0}}), .out(transistor_3_out), .gate(not_5_out));
  and and_8 (and_8_out, and_3_out, sequencer_2_out_5);
  Transistor #(.\type ("n"), .width(16)) transistor_5 (
    .in({15'h400, compare_1_out_2[0]}), .out(transistor_3_out), .gate(and_8_out));
  and and_9 (and_9_out, and_6_out, decoder_1_out3);
  sequencer sequencer_2 (
    .in_1(nand_1_out), .out_3(sequencer_2_out_3), .out_4(sequencer_2_out_4), .out_5(sequencer_2_out_5),
    .out_6(sequencer_2_out_6), .in_2(and_4_out));
  Transistor #(.\type ("n"), .width(16)) transistor_6 (.in(transistor_9_out), .out(transistor_3_out), .gate(or_4_out));
  Transistor #(.\type ("n"), .width(8)) transistor_7 (
    .in(register_3_out_2), .out(transistor_7_out), .gate(sequencer_1_out_3));
  not not_6 (not_6_out, sequencer_1_out_3);
  Transistor #(.\type ("n"), .width(8)) transistor_8 (.in({8{1'b0}}), .out(transistor_7_out), .gate(not_6_out));
  Transistor #(.\type ("n"), .width(16)) transistor_9 (
    .in({5'b00001, rom_1_data_4, register_5_q[15:8]}), .out(transistor_9_out), .gate(and_11_out));
  or or_4 (or_4_out, sequencer_2_out_5, and_11_out, or_5_out);
  and and_10 (and_10_out, decoder_1_out0, sequencer_2_out_5);
  and and_11 (and_11_out, decoder_1_out1, sequencer_2_out_5);
  Transistor #(.\type ("n"), .width(16)) transistor_10 (
    .in({5'b00001, rom_1_data[2:0], ALU_out_3}), .out(transistor_9_out), .gate(and_10_out));
  register register_3 (.in_1(transistor_3_out), .out_2(register_3_out_2));
  Transistor #(.\type ("n"), .width(16)) transistor_11 (
    .in({rom_1_data_3, {8{1'b0}}}), .out(transistor_9_out), .gate(and_12_out));
  Transistor #(.\type ("n"), .width(16)) transistor_12 (
    .in({rom_1_data_5, rom_1_data_4, {8{1'b0}}}), .out(transistor_9_out), .gate(and_14_out));
  or or_5 (or_5_out, and_10_out, and_12_out, and_14_out);
  and and_12 (and_12_out, rom_1_data[29], sequencer_2_out_3);
  not not_7 (not_7_out, rom_1_data[29]);
  and and_13 (and_13_out, not_7_out, sequencer_2_out_3);
  Transistor #(.\type ("n"), .width(8)) transistor_13 (.in(rom_1_data_3), .out(transistor_13_out), .gate(and_13_out));
  Transistor #(.\type ("n"), .width(8)) transistor_14 (
    .in(register_3_out_2), .out(transistor_13_out), .gate(and_12_out));
  and and_14 (and_14_out, rom_1_data[28], sequencer_2_out_4);
  not not_8 (not_8_out, rom_1_data[28]);
  and and_15 (and_15_out, not_8_out, sequencer_2_out_4);
  Transistor #(.\type ("n"), .width(8)) transistor_15 (
    .in({rom_1_data_5, rom_1_data_4}), .out(transistor_15_out), .gate(and_15_out));
  Transistor #(.\type ("n"), .width(8)) transistor_16 (
    .in(register_3_out_2), .out(transistor_15_out), .gate(and_14_out));
  Register register_4 (.D(transistor_13_out), .Q(register_5_q[15:8]), .clk(clock_1_out));  // open: en, clr
  Register register_5 (.D(transistor_15_out), .Q(register_5_q[7:0]), .clk(clock_1_out));  // open: en, clr

  // Notes on the sheet:
  //   contents of rom_1 (hex, n*v repeats v):
  //   50060000 50080100 50000200 25000100 34010202 c5030000 c3080000 88000000 c3070000
endmodule

module ALU (
  input  [23:0] in_1,
  output out_2,
  output [7:0] out_3
);

  wire decoder_1_out0, decoder_1_out1, decoder_1_out2, decoder_1_out3, decoder_1_out4, decoder_1_out5,
       not_2_out;
  wire [7:0] adder_1_out, and_1_out, not_1_out, or_1_out, subtractor_1_out, transistor_1_out, xor_1_out;

  Decoder #(.select(3)) decoder_1 (
    .out0(decoder_1_out0), .out1(decoder_1_out1), .out2(decoder_1_out2), .out3(decoder_1_out3),
    .out4(decoder_1_out4), .out5(decoder_1_out5), .sel(in_1[18:16]));  // open: out6, out7, en
  assign or_1_out = in_1[15:8] | in_1[7:0];  // OR_Gate or_1, 8 bits wide
  assign and_1_out = in_1[15:8] & in_1[7:0];  // AND_Gate and_1, 8 bits wide
  assign xor_1_out = in_1[15:8] ^ in_1[7:0];  // XOR_Gate xor_1, 8 bits wide
  Adder adder_1 (.a(in_1[15:8]), .b(in_1[7:0]), .out(adder_1_out), .cout(out_2));  // open: cin
  Subtractor subtractor_1 (.a(in_1[15:8]), .b(in_1[7:0]), .out(subtractor_1_out));  // open: bin, bout
  Transistor #(.\type ("n"), .width(8)) transistor_1 (.in(in_1[15:8]), .out(transistor_1_out), .gate(decoder_1_out0));
  Transistor #(.\type ("n"), .width(8)) transistor_2 (.in(or_1_out), .out(transistor_1_out), .gate(decoder_1_out1));
  Transistor #(.\type ("n"), .width(8)) transistor_3 (.in(and_1_out), .out(transistor_1_out), .gate(decoder_1_out2));
  Transistor #(.\type ("n"), .width(8)) transistor_4 (.in(xor_1_out), .out(transistor_1_out), .gate(decoder_1_out3));
  Transistor #(.\type ("n"), .width(8)) transistor_5 (.in(adder_1_out), .out(transistor_1_out), .gate(decoder_1_out4));
  Transistor #(.\type ("n"), .width(8)) transistor_6 (
    .in(subtractor_1_out), .out(transistor_1_out), .gate(decoder_1_out5));
  assign not_1_out = ~transistor_1_out;  // NOT_Gate not_1, 8 bits wide
  not not_2 (not_2_out, in_1[19]);
  Transistor #(.\type ("n"), .width(8)) transistor_7 (.in(transistor_1_out), .out(out_3), .gate(not_2_out));
  Transistor #(.\type ("n"), .width(8)) transistor_8 (.in(not_1_out), .out(out_3), .gate(in_1[19]));

  // Notes on the sheet:
  //   A
  //   B
endmodule

module register (
  input  [15:0] in_1,
  output [7:0] out_2
);

  wire and_1_out, and_2_out, and_3_out, and_4_out, and_5_out, and_6_out, and_7_out, and_8_out, and_9_out,
       and_10_out, and_11_out, and_12_out, and_13_out, and_14_out, and_15_out, and_16_out, clock_1_out,
       decoder_1_out0, decoder_1_out1, decoder_1_out2, decoder_1_out3, decoder_1_out4, decoder_1_out5,
       decoder_1_out6, decoder_1_out7, not_1_out, not_2_out, not_3_out, not_4_out, not_5_out, not_6_out,
       not_7_out, not_8_out;
  wire [7:0] R1_q, R2_q, R3_q, R4_q, R5_q, R6_q, R7_q, R8_q, transistor_2_out, transistor_4_out,
       transistor_5_out, transistor_6_out, transistor_9_out, transistor_10_out, transistor_13_out,
       transistor_14_out;

  Clock clock_1 (.out(clock_1_out));
  Decoder #(.select(3)) decoder_1 (
    .out0(decoder_1_out0), .out1(decoder_1_out1), .out2(decoder_1_out2), .out3(decoder_1_out3),
    .out4(decoder_1_out4), .out5(decoder_1_out5), .out6(decoder_1_out6), .out7(decoder_1_out7),
    .sel(in_1[10:8]));  // open: en
  and and_1 (and_1_out, decoder_1_out0, in_1[11]);
  and and_2 (and_2_out, decoder_1_out4, in_1[11]);
  not not_1 (not_1_out, in_1[11]);
  and and_3 (and_3_out, decoder_1_out0, not_1_out);
  Transistor #(.\type ("n"), .width(8)) transistor_1 (.in(R1_q), .out(out_2), .gate(and_3_out));
  Transistor #(.\type ("n"), .width(8)) transistor_2 (.in(in_1[7:0]), .out(transistor_2_out), .gate(and_1_out));
  Register R1 (.D(transistor_2_out), .Q(R1_q), .clk(clock_1_out));  // open: en, clr
  not not_2 (not_2_out, in_1[11]);
  and and_4 (and_4_out, decoder_1_out4, not_2_out);
  Register R5 (.D(transistor_4_out), .Q(R5_q), .clk(clock_1_out));  // open: en, clr
  Transistor #(.\type ("n"), .width(8)) transistor_3 (.in(R5_q), .out(out_2), .gate(and_4_out));
  Transistor #(.\type ("n"), .width(8)) transistor_4 (.in(in_1[7:0]), .out(transistor_4_out), .gate(and_2_out));
  and and_5 (and_5_out, decoder_1_out1, in_1[11]);
  and and_6 (and_6_out, decoder_1_out5, in_1[11]);
  not not_3 (not_3_out, in_1[11]);
  and and_7 (and_7_out, decoder_1_out1, not_3_out);
  Register R2 (.D(transistor_5_out), .Q(R2_q), .clk(clock_1_out));  // open: en, clr
  Transistor #(.\type ("n"), .width(8)) transistor_5 (.in(in_1[7:0]), .out(transistor_5_out), .gate(and_5_out));
  not not_4 (not_4_out, in_1[11]);
  and and_8 (and_8_out, decoder_1_out5, not_4_out);
  Transistor #(.\type ("n"), .width(8)) transistor_6 (.in(in_1[7:0]), .out(transistor_6_out), .gate(and_6_out));
  Register R6 (.D(transistor_6_out), .Q(R6_q), .clk(clock_1_out));  // open: en, clr
  Transistor #(.\type ("n"), .width(8)) transistor_7 (.in(R2_q), .out(out_2), .gate(and_7_out));
  Transistor #(.\type ("n"), .width(8)) transistor_8 (.in(R6_q), .out(out_2), .gate(and_8_out));
  and and_9 (and_9_out, decoder_1_out2, in_1[11]);
  and and_10 (and_10_out, decoder_1_out2, not_5_out);
  Register R3 (.D(transistor_9_out), .Q(R3_q), .clk(clock_1_out));  // open: en, clr
  Transistor #(.\type ("n"), .width(8)) transistor_9 (.in(in_1[7:0]), .out(transistor_9_out), .gate(and_9_out));
  and and_11 (and_11_out, decoder_1_out6, in_1[11]);
  and and_12 (and_12_out, decoder_1_out6, not_6_out);
  Transistor #(.\type ("n"), .width(8)) transistor_10 (.in(in_1[7:0]), .out(transistor_10_out), .gate(and_11_out));
  Register R7 (.D(transistor_10_out), .Q(R7_q), .clk(clock_1_out));  // open: en, clr
  not not_5 (not_5_out, in_1[11]);
  Transistor #(.\type ("n"), .width(8)) transistor_11 (.in(R3_q), .out(out_2), .gate(and_10_out));
  not not_6 (not_6_out, in_1[11]);
  Transistor #(.\type ("n"), .width(8)) transistor_12 (.in(R7_q), .out(out_2), .gate(and_12_out));
  and and_13 (and_13_out, decoder_1_out3, in_1[11]);
  Register R4 (.D(transistor_13_out), .Q(R4_q), .clk(clock_1_out));  // open: en, clr
  Transistor #(.\type ("n"), .width(8)) transistor_13 (.in(in_1[7:0]), .out(transistor_13_out), .gate(and_13_out));
  and and_14 (and_14_out, decoder_1_out7, in_1[11]);
  Transistor #(.\type ("n"), .width(8)) transistor_14 (.in(in_1[7:0]), .out(transistor_14_out), .gate(and_14_out));
  Register R8 (.D(transistor_14_out), .Q(R8_q), .clk(clock_1_out));  // open: en, clr
  not not_7 (not_7_out, in_1[11]);
  and and_15 (and_15_out, decoder_1_out3, not_7_out);
  Transistor #(.\type ("n"), .width(8)) transistor_15 (.in(R4_q), .out(out_2), .gate(and_15_out));
  not not_8 (not_8_out, in_1[11]);
  and and_16 (and_16_out, decoder_1_out7, not_8_out);
  Transistor #(.\type ("n"), .width(8)) transistor_16 (.in(R8_q), .out(out_2), .gate(and_16_out));
endmodule

module append (
  input  [7:0] in_1,
  input  [7:0] in_2,
  input  in_3,
  output [15:0] out_4
);

  wire not_1_out;
  wire [15:0] bit_extender_1_out, bit_extender_2_out, bit_extender_3_out, multiplier_1_out, transistor_1_out;

  Transistor #(.\type ("n"), .width(16)) transistor_1 (.in({16{1'b0}}), .out(transistor_1_out), .gate(in_3));
  assign bit_extender_1_out = {{8{1'b0}}, in_2};  // Bit_Extender bit_extender_1
  not not_1 (not_1_out, in_3);
  Transistor #(.width(16)) transistor_2 (.in(bit_extender_1_out), .out(transistor_1_out), .gate(not_1_out));
  assign bit_extender_2_out = {{7{1'b0}}, 9'h100};  // Bit_Extender bit_extender_2
  assign bit_extender_3_out = {{8{1'b0}}, in_1};  // Bit_Extender bit_extender_3
  Multiplier #(.width(16)) multiplier_1 (
    .a(bit_extender_2_out), .b(bit_extender_3_out), .out(multiplier_1_out));  // open: cin, cout
  assign out_4 = multiplier_1_out | transistor_1_out;  // OR_Gate or_1, 16 bits wide

  // Notes on the sheet:
  //   Give a both 8 bits cocatenated on 16 bits a + b
endmodule

module sanbox (
  input  [31:0] in_1,
  input  [7:0] in_2,
  input  in_3,
  input  [7:0] in_4,
  input  [31:0] in_5,
  output [7:0] out_6
);

  wire and_1_out, button_1_out, button_2_out, button_3_out, button_4_out, clock_1_out, j_k_ff_1_q,
       j_k_ff_3_q, j_k_ff_4_q, j_k_ff_5_q, j_k_ff_6_q, j_k_ff_7_q, j_k_ff_8_q, j_k_ff_9_q, not_1_out,
       not_2_out, not_3_out, transistor_4_out, undriven_2;
  wire [7:0] ram_1_data, register_2_q;
  wire [31:0] multiplier_1_out, register_1_q, rom_1_data, undriven;

  Clock clock_1 (.out(clock_1_out));
  Button button_1 (.out(button_1_out));
  Button button_2 (.out(button_2_out));
  Transistor #(.\type ("n"), .width(32)) transistor_1 (.in(undriven));  // open: out, gate
  Register #(.width(32)) register_1 (.D(multiplier_1_out), .Q(register_1_q), .clk(clock_1_out));  // open: en, clr
  J_K_Flip_Flop j_k_ff_1 (
    .J(button_1_out), .clk(clock_1_out), .K(1'b1), .Q(j_k_ff_1_q), .reset(undriven_2));  // open: Qn, preset, en
  Button button_3 (.out(button_3_out));
  Multiplier #(.width(32)) multiplier_1 (.a(register_1_q), .b(32'h2), .out(multiplier_1_out));  // open: cin, cout
  J_K_Flip_Flop j_k_ff_2 (.J(j_k_ff_1_q), .clk(clock_1_out), .K(1'b1));  // open: Q, Qn, preset, en, reset
  LED led_1 (.in(j_k_ff_3_q));
  J_K_Flip_Flop j_k_ff_3 (
    .J(button_3_out), .clk(clock_1_out), .K(1'b1), .Q(j_k_ff_3_q));  // open: Qn, preset, en, reset
  Transistor #(.\type ("n"), .width(32)) transistor_2 ();  // open: in, out, gate
  Register register_2 (.Q(register_2_q));  // open: D, en, clk, clr
  LED led_2 (.in(j_k_ff_4_q));
  J_K_Flip_Flop j_k_ff_4 (.J(j_k_ff_3_q), .clk(clock_1_out), .K(1'b1), .Q(j_k_ff_4_q));  // open: Qn, preset, en, reset
  LED led_3 (.in(j_k_ff_5_q));
  J_K_Flip_Flop j_k_ff_5 (.J(j_k_ff_4_q), .clk(clock_1_out), .K(1'b1), .Q(j_k_ff_5_q));  // open: Qn, preset, en, reset
  LED led_4 (.in(j_k_ff_6_q));
  J_K_Flip_Flop j_k_ff_6 (.J(j_k_ff_5_q), .clk(clock_1_out), .K(1'b1), .Q(j_k_ff_6_q));  // open: Qn, preset, en, reset
  ROM #(.dataWidth(32)) rom_1 (.addr(register_2_q), .data(rom_1_data));  // open: sel
  LED led_5 (.in(j_k_ff_7_q));
  J_K_Flip_Flop j_k_ff_7 (.J(j_k_ff_6_q), .clk(clock_1_out), .K(1'b1), .Q(j_k_ff_7_q));  // open: Qn, preset, en, reset
  Transistor transistor_3 (.in(1'b1), .gate(button_2_out));  // open: out
  Transistor transistor_4 (.in(in_3), .out(transistor_4_out), .gate(button_2_out));
  // DotMatrix #(.inputtype("select"), .matrixcols(32), .matrixrows(32)) dotmatrix_1: pin names not known; wires that end beside it: register_1_q, in_5
  LED led_6 (.in(j_k_ff_8_q));
  J_K_Flip_Flop j_k_ff_8 (
    .J(and_1_out), .clk(clock_1_out), .K(not_1_out), .Q(j_k_ff_8_q));  // open: Qn, preset, en, reset
  and and_1 (and_1_out, button_2_out, not_1_out);
  not not_1 (not_1_out, j_k_ff_9_q);
  LED led_7 (.in(j_k_ff_9_q));
  J_K_Flip_Flop j_k_ff_9 (
    .J(j_k_ff_8_q), .clk(clock_1_out), .K(not_2_out), .Q(j_k_ff_9_q));  // open: Qn, preset, en, reset
  not not_2 (not_2_out, button_2_out);
  Button button_4 (.out(button_4_out));
  Transistor #(.\type ("n"), .width(8)) transistor_5 (.in(ram_1_data), .out(out_6), .gate(button_4_out));
  RAM ram_1 (.addr(in_2), .data(ram_1_data), .sel(1'b1), .clk(clock_1_out), .ld(button_4_out));  // open: clr
  not not_3 (not_3_out, button_4_out);
  Transistor #(.\type ("n"), .width(8)) transistor_6 (.in(in_4), .out(ram_1_data), .gate(not_3_out));

  // Notes on the sheet:
  //   contents of rom_1 (hex, n*v repeats v):
  //   54030700
endmodule

module sequencer (
  input  in_1,
  input  in_2,
  output out_3,
  output out_4,
  output out_5,
  output out_6
);

  wire and_1_out, clock_1_out, j_k_ff_5_q, nor_1_out, not_1_out, or_1_out;

  Clock clock_1 (.out(clock_1_out));
  and and_1 (and_1_out, in_1, nor_1_out);
  J_K_Flip_Flop j_k_ff_1 (.J(and_1_out), .clk(clock_1_out), .K(nor_1_out), .Q(out_3));  // open: Qn, preset, en, reset
  not not_1 (not_1_out, in_1);
  J_K_Flip_Flop j_k_ff_2 (.J(out_3), .clk(clock_1_out), .K(1'b1), .Q(out_4));  // open: Qn, preset, en, reset
  J_K_Flip_Flop j_k_ff_3 (.J(out_4), .clk(clock_1_out), .K(1'b1), .Q(out_5));  // open: Qn, preset, en, reset
  J_K_Flip_Flop j_k_ff_4 (.J(out_5), .clk(clock_1_out), .K(1'b1), .Q(out_6));  // open: Qn, preset, en, reset
  or or_1 (or_1_out, not_1_out, out_6);
  nor nor_1 (nor_1_out, j_k_ff_5_q, in_2);
  J_K_Flip_Flop j_k_ff_5 (.J(out_3), .clk(clock_1_out), .K(or_1_out), .Q(j_k_ff_5_q));  // open: Qn, preset, en, reset
endmodule

module iterator (
  input  in_1,
  input  in_2,
  input  [7:0] in_3,
  output [7:0] out_4
);

  wire and_1_out, clock_1_out, comparator_1_lt, not_1_out, or_1_out;

  Clock clock_1 (.out(clock_1_out));
  and and_1 (and_1_out, clock_1_out, in_1);
  or or_1 (or_1_out, and_1_out, in_2);
  Counter counter_1 (.Q(out_4), .clk(or_1_out), .clr(not_1_out));  // open: load, D, count, carry
  Comparator comparator_1 (.a(out_4), .b(in_3), .lt(comparator_1_lt));  // open: gt, eq
  not not_1 (not_1_out, comparator_1_lt);
endmodule

module compare (
  input  [23:0] in_1,
  output out_2
);

  wire comparator_1_eq, comparator_1_gt, comparator_1_lt, decoder_1_out0, decoder_1_out1, decoder_1_out2,
       decoder_1_out3, not_1_out, not_2_out, transistor_1_out;

  Decoder #(.select(2)) decoder_1 (
    .out0(decoder_1_out0), .out1(decoder_1_out1), .out2(decoder_1_out2), .out3(decoder_1_out3),
    .sel(in_1[17:16]));  // open: en
  Comparator comparator_1 (
    .a(in_1[15:8]), .b(in_1[7:0]), .gt(comparator_1_gt), .eq(comparator_1_eq), .lt(comparator_1_lt));
  Transistor #(.\type ("n")) transistor_1 (.in(comparator_1_gt), .out(transistor_1_out), .gate(decoder_1_out0));
  Transistor #(.\type ("n")) transistor_2 (.in(comparator_1_eq), .out(transistor_1_out), .gate(decoder_1_out1));
  Transistor #(.\type ("n")) transistor_3 (.in(comparator_1_lt), .out(transistor_1_out), .gate(decoder_1_out2));
  Transistor #(.\type ("n")) transistor_4 (.in(1'b0), .out(transistor_1_out), .gate(decoder_1_out3));
  not not_1 (not_1_out, in_1[18]);
  Transistor #(.\type ("n")) transistor_5 (.in(transistor_1_out), .out(out_2), .gate(not_1_out));
  Transistor #(.\type ("n")) transistor_6 (.in(not_2_out), .out(out_2), .gate(in_1[18]));
  not not_2 (not_2_out, transistor_1_out);
endmodule

module memory (
  input  [7:0] in_1,
  input  [7:0] in_2,
  input  in_3,
  output [7:0] out_4
);

  wire clock_1_out, not_1_out;
  wire [7:0] ram_1_data;

  Clock clock_1 (.out(clock_1_out));
  RAM ram_1 (.addr(in_1), .data(ram_1_data), .sel(1'b1), .clk(clock_1_out), .ld(in_3));  // open: clr
  not not_1 (not_1_out, in_3);
  Transistor #(.\type ("n"), .width(8)) transistor_1 (.in(in_2), .out(ram_1_data), .gate(not_1_out));
  Transistor #(.\type ("n"), .width(8)) transistor_2 (.in(ram_1_data), .out(out_4), .gate(in_3));
endmodule
